// Logisim project ALUs.circ as structural Verilog: 3 circuits, main circuit Lowest ALU
// ALU
module Lowest_ALU (
  input  [1:0] Operation,
  input  a,
  input  Binvert,
  input  b,
  output Result,
  output CarryOut
);

  wire adder_1_out, AND_out, multiplexer_1_out, NOT_out, OR_out;

  not NOT (NOT_out, b);
  Multiplexer multiplexer_1 (.in0(b), .in1(NOT_out), .out(multiplexer_1_out), .sel(Binvert));  // open: en
  and AND (AND_out, a, multiplexer_1_out);
  or OR (OR_out, a, multiplexer_1_out);
  Adder #(.width(1)) adder_1 (.a(a), .b(multiplexer_1_out), .out(adder_1_out), .cin(Binvert), .cout(CarryOut));
  Multiplexer #(.select(2)) multiplexer_2 (
    .in0(AND_out), .in1(OR_out), .in2(adder_1_out), .out(Result), .sel(Operation));  // open: in3, en
endmodule

module ALU (
  input  [1:0] in_1,
  input  in_2,
  input  in_3,
  input  in_4,
  input  in_5,
  input  in_6,
  input  in_7,
  input  in_8,
  input  in_9,
  input  in_10,
  input  in_11,
  input  in_12,
  input  in_13,
  input  in_14,
  input  in_15,
  input  in_16,
  input  in_17,
  input  in_18,
  output out_19,
  output out_20,
  output out_21,
  output out_22,
  output out_23,
  output out_24,
  output out_25,
  output out_26,
  output out_27
);

  wire lowest_alu_1_carryout, n1b_alu_1_carryout, n1b_alu_2_carryout, n1b_alu_3_carryout, n1b_alu_4_carryout,
       n1b_alu_5_carryout, n1b_alu_6_carryout;

  Lowest_ALU lowest_alu_1 (
    .a(in_3), .Binvert(in_2), .b(in_4), .Result(out_19), .CarryOut(lowest_alu_1_carryout), .Operation(in_1));
  _1b_ALU u_1b_alu_1 (
    .a(in_5), .Cin(lowest_alu_1_carryout), .b(in_6), .Result(out_20), .CarryOut(n1b_alu_1_carryout),
    .Binvert(in_2), .Operation(in_1));
  _1b_ALU u_1b_alu_2 (
    .a(in_7), .Cin(n1b_alu_1_carryout), .b(in_8), .Result(out_21), .CarryOut(n1b_alu_2_carryout),
    .Binvert(in_2), .Operation(in_1));
  _1b_ALU u_1b_alu_3 (
    .a(in_9), .Cin(n1b_alu_2_carryout), .b(in_10), .Result(out_22), .CarryOut(n1b_alu_3_carryout),
    .Binvert(in_2), .Operation(in_1));
  _1b_ALU u_1b_alu_4 (
    .a(in_11), .Cin(n1b_alu_3_carryout), .b(in_12), .Result(out_23), .CarryOut(n1b_alu_4_carryout),
    .Binvert(in_2), .Operation(in_1));
  _1b_ALU u_1b_alu_5 (
    .a(in_13), .Cin(n1b_alu_4_carryout), .b(in_14), .Result(out_24), .CarryOut(n1b_alu_5_carryout),
    .Binvert(in_2), .Operation(in_1));
  _1b_ALU u_1b_alu_6 (
    .a(in_15), .Cin(n1b_alu_5_carryout), .b(in_16), .Result(out_25), .CarryOut(n1b_alu_6_carryout),
    .Binvert(in_2), .Operation(in_1));
  _1b_ALU u_1b_alu_7 (
    .a(in_17), .Cin(n1b_alu_6_carryout), .b(in_18), .Result(out_26), .CarryOut(out_27), .Binvert(in_2),
    .Operation(in_1));
endmodule

// ALU
module _1b_ALU (
  input  Binvert,
  input  Cin,
  input  [1:0] Operation,
  input  a,
  input  b,
  output Result,
  output CarryOut
);

  wire adder_1_out, AND_out, multiplexer_1_out, NOT_out, OR_out;

  not NOT (NOT_out, b);
  Multiplexer multiplexer_1 (.in0(b), .in1(NOT_out), .out(multiplexer_1_out), .sel(Binvert));  // open: en
  and AND (AND_out, a, multiplexer_1_out);
  or OR (OR_out, a, multiplexer_1_out);
  Adder #(.width(1)) adder_1 (.a(a), .b(multiplexer_1_out), .out(adder_1_out), .cin(Cin), .cout(CarryOut));
  Multiplexer #(.select(2)) multiplexer_2 (
    .in0(AND_out), .in1(OR_out), .in2(adder_1_out), .out(Result), .sel(Operation));  // open: in3, en
endmodule
